// Logisim project main.circ as structural Verilog: 3 circuits, main circuit main
module main (
);

  wire clock_1_out;
  wire [7:0] register_1_q, undriven;

  Clock clock_1 (.out(clock_1_out));
  Register register_1 (.D(undriven), .Q(register_1_q), .clk(clock_1_out));  // open: en, clr
  fetch_cicuit fetch_cicuit_1 (.in_1(register_1_q));  // open: out_2, out_3, out_4, out_5

  // Notes on the sheet:
  //   new_pc
  //   pc
endmodule

module fetch_cicuit (
  input  [7:0] in_1,
  output [1:0] out_2,
  output [4:0] out_3,
  output out_4,
  output out_5
);

  ROM rom_1 (.addr(in_1), .data({out_2, out_5, out_3}));  // open: sel
  not not_1 (out_4, out_5);

  // Notes on the sheet:
  //   contents of rom_1 (hex, n*v repeats v):
  //   40 0 0 0 69 0 0 0 e0 4*0 b2 41 0 0 0 6a 0 0 0 f0 4*0 b3 42 0 0 0 6b 0 0 0 f0 4*0 b4 43 0 0 0 6c 0 0
  //   0 f0 4*0 b5 44 0 0 0 6d 0 0 0 f0 4*0 b6 45 0 0 0 6e 0 0 0 f0 4*0 b7 46 0 0 0 6f 0 0 0 f0 4*0 b8 47 0
  //   0 0 70 0 0 0 f0 4*0 b9 48 0 0 0 71 0 0 0 f0 4*0 ba
endmodule

module fetch_register (
  input  [1:0] ifun,
  input  [4:0] address,
  input  rax_on,
  input  rbx_on
);
endmodule
